// Logisim project additionneurs.circ as structural Verilog: 5 circuits, main circuit incrementation 3 bits
module incrementation_3_bits (
  input  retenue,
  input  [2:0] x,
  output [2:0] x_retenue,
  output Retenue_2
);

  wire additionneur_retenue_1b_1_propage, additionneur_retenue_1b_2_propage,
       additionneur_retenue_1b_3_propage, and_1_out, and_2_out;

  additionneur_retenue_1b additionneur_retenue_1b_1 (
    .retenue(retenue), .x(x[0]), .x_y(x_retenue[0]), .propage(additionneur_retenue_1b_1_propage));
  additionneur_retenue_1b additionneur_retenue_1b_2 (
    .retenue(and_1_out), .x(x[1]), .x_y(x_retenue[1]), .propage(additionneur_retenue_1b_2_propage));
  and and_1 (and_1_out, additionneur_retenue_1b_1_propage, retenue);
  additionneur_retenue_1b additionneur_retenue_1b_3 (
    .retenue(and_2_out), .x(x[2]), .x_y(x_retenue[2]), .propage(additionneur_retenue_1b_3_propage));
  and and_2 (and_2_out, and_1_out, additionneur_retenue_1b_2_propage);
  and and_3 (Retenue_2, and_2_out, additionneur_retenue_1b_3_propage);

  // Notes on the sheet:
  //   N'additionne que la retenue. 6 portes
endmodule

module additionneur_retenue_1b (
  input  retenue,
  input  x,
  output x_y,
  output propage
);

  xor xor_1 (x_y, retenue, x);

  assign propage = x;
endmodule

module decrementeur_3bits (
  input  \annule_décrémentation ,
  input  [2:0] x,
  output [2:0] x_y_retenue,
  output Overflow
);

  wire decrementeur_1b_optimise_1_genere, decrementeur_1b_optimise_2_genere,
       decrementeur_1b_optimise_3_genere, or_1_out, or_2_out, or_3_out, or_4_out, or_5_out;

  decrementeur_1b_optimise decrementeur_1b_optimise_1 (
    .retenue(\annule_décrémentation ), .x(x[0]), .x_y(x_y_retenue[0]),
    .genere(decrementeur_1b_optimise_1_genere));
  decrementeur_1b_optimise decrementeur_1b_optimise_2 (
    .retenue(or_1_out), .x(x[1]), .x_y(x_y_retenue[1]), .genere(decrementeur_1b_optimise_2_genere));
  decrementeur_1b_optimise decrementeur_1b_optimise_3 (
    .retenue(or_3_out), .x(x[2]), .x_y(x_y_retenue[2]), .genere(decrementeur_1b_optimise_3_genere));
  or or_1 (or_1_out, decrementeur_1b_optimise_1_genere, \annule_décrémentation );
  or or_2 (or_2_out, \annule_décrémentation , decrementeur_1b_optimise_1_genere);
  or or_3 (or_3_out, or_2_out, decrementeur_1b_optimise_2_genere);
  or or_4 (or_4_out, \annule_décrémentation , decrementeur_1b_optimise_1_genere);
  or or_5 (or_5_out, decrementeur_1b_optimise_2_genere, decrementeur_1b_optimise_3_genere);
  nor nor_1 (Overflow, or_4_out, or_5_out);

  // Notes on the sheet:
  //   Décrémenteur à prédiction de retenue. 9 portes
endmodule

module decrementeur_1b_optimise (
  input  retenue,
  input  x,
  output x_y,
  output genere
);

  xnor xnor_1 (x_y, retenue, x);

  assign genere = x;
endmodule

module alu (
  input  Overflow,
  input  Ignore_overflow,
  input  _1_si_NOT__0_si_INC_DEC,
  input  _1_si_INC__0_si_DEC,
  input  [2:0] in,
  output Overflow_out,
  output [2:0] out,
  output Zero_Flag_out
);

  wire and_1_out, and_2_out, and_3_out, \Décrémenteur_overflow , \Incrémenteur_retenue_2 , nand_1_out,
       nor_1_out, nor_2_out, or_1_out, or_2_out;
  wire [0:0] xor_1_out;
  wire [2:0] \Décrémenteur_x_y_retenue , \Incrémenteur_x_retenue ;

  nor nor_1 (nor_1_out, Overflow, Ignore_overflow);
  or or_1 (or_1_out, Overflow, Ignore_overflow);
  and and_1 (and_1_out, or_1_out, _1_si_NOT__0_si_INC_DEC);
  and and_2 (and_2_out, _1_si_NOT__0_si_INC_DEC, Ignore_overflow);
  nand nand_1 (nand_1_out, or_1_out, _1_si_NOT__0_si_INC_DEC);
  xor xor_1 (xor_1_out[0], and_2_out, in[0]);
  nor nor_2 (nor_2_out, _1_si_INC__0_si_DEC, and_1_out);
  and and_3 (and_3_out, _1_si_INC__0_si_DEC, nand_1_out);
  incrementation_3_bits \Incrémenteur  (
    .retenue(or_1_out), .x(in), .x_retenue(\Incrémenteur_x_retenue ), .Retenue_2(\Incrémenteur_retenue_2 ));
  decrementeur_3bits \Décrémenteur  (
    .\annule_décrémentation (nor_1_out), .x(in), .x_y_retenue(\Décrémenteur_x_y_retenue ),
    .Overflow(\Décrémenteur_overflow ));
  or or_2 (or_2_out, in[1], in[0]);
  Transistor #(.\type ("n")) transistor_1 (.in(\Décrémenteur_overflow ), .out(Overflow_out), .gate(nor_2_out));
  Transistor #(.\type ("n"), .width(3)) transistor_2 (.in(\Décrémenteur_x_y_retenue ), .out(out), .gate(nor_2_out));
  nor nor_3 (Zero_Flag_out, or_2_out, in[2]);
  Transistor #(.\type ("n")) transistor_3 (.in(\Incrémenteur_retenue_2 ), .out(Overflow_out), .gate(and_3_out));
  Transistor #(.\type ("n"), .width(3)) transistor_4 (.in(\Incrémenteur_x_retenue ), .out(out), .gate(and_3_out));
  Transistor #(.\type ("n"), .width(3)) transistor_5 (.in({in[2:1], xor_1_out[0]}), .out(out), .gate(and_1_out));
endmodule
